// Logisim project ULA.circ as structural Verilog: 4 circuits, main circuit main
module main (
  input  B,
  input  A,
  input  X0,
  input  X1,
  input  X2,
  input  Enabled,
  output Igual,
  output Ts,
  output F0
);

  wire comparador_1_s0, somadorcomplemento2_1_s0;

  SomadorComplemento2 somadorcomplemento2_1 (.B(B), .A(A), .TE(X0), .S0(somadorcomplemento2_1_s0), .TS(Ts));
  Multiplexer multiplexer_1 (.in0(somadorcomplemento2_1_s0), .in1(comparador_1_s0), .out(F0), .sel(X1), .en(Enabled));
  Comparador comparador_1 (.Habilita(X0), .X2(X2), .B(B), .A(A), .Igual(Igual), .S0(comparador_1_s0));

  // Notes on the sheet:
  //   X0 = 0 : Adiçao
  //   X0 = 1 : Subtração
  //   X1 = 0 : Subtracao ou Adicao
  //   X1 = 1 : Igualdade ou menor que
  //   X2 = 0 : Menor
  //   X2 = 1 : Igual
endmodule

module SomadorComplemento2 (
  input  B,
  input  A,
  input  TE,
  output S0,
  output TS
);

  wire xor_1_out;

  xor xor_1 (xor_1_out, B, TE);
  Somador Somador (.A(A), .B(xor_1_out), .Te(TE), .S0(S0), .TS(TS));

  // Notes on the sheet:
  //   B é o bit mais significativo (a esquerda)
endmodule

module Somador (
  input  A,
  input  B,
  input  Te,
  output S0,
  output TS
);

  wire and_1_out, and_2_out, and_3_out, xor_1_out;

  and and_1 (and_1_out, A, B);
  and and_2 (and_2_out, A, Te);
  and and_3 (and_3_out, B, Te);
  xor xor_1 (xor_1_out, B, Te);
  or or_1 (TS, and_1_out, and_2_out, and_3_out);
  xor xor_2 (S0, A, xor_1_out);
endmodule

module Comparador (
  input  Habilita,
  input  B,
  input  A,
  input  X2,
  output Igual,
  output S0
);

  wire and_1_out, and_2_out, not_1_out, xnor_1_out;

  xnor xnor_1 (xnor_1_out, B, A);
  not not_1 (not_1_out, B);
  and and_1 (and_1_out, not_1_out, A);
  and and_2 (and_2_out, and_1_out, Habilita);
  Multiplexer multiplexer_1 (.in0(and_2_out), .in1(Igual), .out(S0), .sel(X2), .en(Habilita));
  and and_3 (Igual, xnor_1_out, Habilita);

  // Notes on the sheet:
  //   0 - Menor
  //   1 - Igual
endmodule
